// Logisim project 4BIT AU.circ as structural Verilog
module SINGLE_BIT_ALU (
  input  Cin,
  input  A0,
  input  B0,
  input  Constant1,
  input  S0,
  input  S1,
  output D0,
  output Carry_Out
);

  wire main_1_out_7, not_1_out, not_2_out;

  not not_1 (not_1_out, B0);
  not not_2 (not_2_out, Constant1);
  _4INTO1_MUX_main main_1 (
    .D0(B0), .D1(not_1_out), .D2(Constant1), .D3(not_2_out), .S0(S0), .S1(S1), .out_7(main_1_out_7));
  _4INTO1_MUX_FA fa_1 (.in_1(Cin), .in_2(A0), .in_3(main_1_out_7), .out_4(D0), .out_5(Carry_Out));
endmodule

module _4_BIT_AU (
  input  Cin,
  input  [3:0] B3B2B1B0,
  input  [3:0] A3A2A1A0,
  input  [3:0] Constant,
  input  in_5,
  input  in_6,
  output [3:0] out_7,
  output OVERFLOW,
  output CarryCut
);

  wire single_bit_alu_1_carry_out, single_bit_alu_2_carry_out, single_bit_alu_3_carry_out;

  SINGLE_BIT_ALU single_bit_alu_1 (
    .A0(B3B2B1B0[0]), .B0(A3A2A1A0[0]), .Constant1(Constant[0]), .S0(in_6), .S1(in_5), .Cin(Cin),
    .D0(out_7[0]), .Carry_Out(single_bit_alu_1_carry_out));
  SINGLE_BIT_ALU single_bit_alu_2 (
    .A0(B3B2B1B0[1]), .B0(A3A2A1A0[1]), .Constant1(Constant[1]), .S0(in_6), .S1(in_5),
    .Cin(single_bit_alu_1_carry_out), .D0(out_7[1]), .Carry_Out(single_bit_alu_2_carry_out));
  SINGLE_BIT_ALU single_bit_alu_3 (
    .A0(B3B2B1B0[2]), .B0(A3A2A1A0[2]), .Constant1(Constant[2]), .S0(in_6), .S1(in_5),
    .Cin(single_bit_alu_2_carry_out), .D0(out_7[2]), .Carry_Out(single_bit_alu_3_carry_out));
  SINGLE_BIT_ALU single_bit_alu_4 (
    .A0(B3B2B1B0[3]), .B0(A3A2A1A0[3]), .Constant1(Constant[3]), .S0(in_6), .S1(in_5),
    .Cin(single_bit_alu_3_carry_out), .D0(out_7[3]), .Carry_Out(CarryCut));
  xor xor_1 (OVERFLOW, single_bit_alu_3_carry_out, CarryCut);

  // Notes on the sheet:
  //   D3D2D1D0
endmodule

module FA (
  input  in_1,
  input  in_2,
  input  in_3,
  output out_4,
  output out_5
);

  wire and_1_out, and_2_out, xor_1_out;

  xor xor_1 (xor_1_out, in_1, in_2);
  and and_1 (and_1_out, in_1, in_2);
  and and_2 (and_2_out, xor_1_out, in_3);
  xor xor_2 (out_4, xor_1_out, in_3);
  or or_1 (out_5, and_2_out, and_1_out);
endmodule

module _4BIT_Logic_LU (
  input  [3:0] B3B2B1B0,
  input  S1,
  input  S0,
  input  [3:0] in_4,
  output [3:0] Y3Y2Y1Y0
);

  single_stage_LOGICckt single_stage_logicckt_1 (
    .A0(B3B2B1B0[0]), .in_3(in_4[0]), .S1(S1), .S0(S0), .Y0(Y3Y2Y1Y0[0]));  // open: B0
  single_stage_LOGICckt single_stage_logicckt_2 (
    .A0(B3B2B1B0[1]), .in_3(in_4[1]), .S1(S1), .S0(S0), .Y0(Y3Y2Y1Y0[1]));  // open: B0
  single_stage_LOGICckt single_stage_logicckt_3 (
    .A0(B3B2B1B0[2]), .in_3(in_4[2]), .S1(S1), .S0(S0), .Y0(Y3Y2Y1Y0[2]));  // open: B0
  single_stage_LOGICckt single_stage_logicckt_4 (
    .A0(B3B2B1B0[3]), .in_3(in_4[3]), .S1(S1), .S0(S0), .Y0(Y3Y2Y1Y0[3]));  // open: B0

  // Notes on the sheet:
  //   A3A2A1A0
endmodule

module _2to1MUX (
  input  D0,
  input  D1,
  input  S0,
  output Y
);

  wire nand_1_out, nand_2_out, nand_3_out;

  nand nand_1 (nand_1_out, S0, S0);
  nand nand_2 (nand_2_out, nand_1_out, D0);
  nand nand_3 (nand_3_out, S0, D1);
  nand nand_4 (Y, nand_2_out, nand_3_out);
endmodule

module _2to1MultibitMux (
  input  [3:0] A,
  input  [3:0] B,
  input  in_3,
  output [3:0] Y
);

  _2to1MUX u_2to1mux_1 (.D0(A[0]), .D1(B[0]), .S0(in_3), .Y(Y[0]));
  _2to1MUX u_2to1mux_2 (.D0(A[1]), .D1(B[1]), .S0(in_3), .Y(Y[1]));
  _2to1MUX u_2to1mux_3 (.D0(A[2]), .D1(B[2]), .S0(in_3), .Y(Y[2]));
  _2to1MUX u_2to1mux_4 (.D0(A[3]), .D1(B[3]), .S0(in_3), .Y(Y[3]));
endmodule

module ALU_4BIT (
  input  [3:0] B,
  input  Cin,
  input  [3:0] A,
  input  S2,
  input  S1,
  input  S0,
  input  [3:0] Constant,
  output Overflow,
  output [3:0] Y,
  output Carry___Sign
);

  wire [3:0] n4_bit_au_1_out_7, n4bit_logic_lu_1_y3y2y1y0;

  _4_BIT_AU u_4_bit_au_1 (
    .Cin(Cin), .B3B2B1B0(B), .A3A2A1A0(A), .Constant(Constant), .in_5(S1), .in_6(S0),
    .out_7(n4_bit_au_1_out_7), .OVERFLOW(Overflow), .CarryCut(Carry___Sign));
  _4BIT_Logic_LU u_4bit_logic_lu_1 (.B3B2B1B0(B), .in_4(A), .S1(S1), .S0(S0), .Y3Y2Y1Y0(n4bit_logic_lu_1_y3y2y1y0));
  _2to1MultibitMux u_2to1multibitmux_1 (.A(n4_bit_au_1_out_7), .B(n4bit_logic_lu_1_y3y2y1y0), .in_3(S2), .Y(Y));

  // Notes on the sheet:
  //   4 bit AU
  //   4 BIT AU
  //   2 to 1multibit MUX
endmodule

module single_stage_LOGICckt (
  input  B0,
  input  A0,
  input  in_3,
  input  S1,
  input  S0,
  output Y0
);

  wire and_1_out, not_1_out, or_1_out, xor_1_out;

  and and_1 (and_1_out, A0, B0);
  or or_1 (or_1_out, B0, B0);
  xor xor_1 (xor_1_out, A0, B0);
  not not_1 (not_1_out, A0);
  _4_to_1_mux u_4_to_1_mux_1 (
    .D0(and_1_out), .D1(or_1_out), .D2(xor_1_out), .D3(not_1_out), .S0(S0), .S1(S1), .out_7(Y0));

  // Notes on the sheet:
  //   MUX
endmodule

module _4_to_1_mux (
  input  D0,
  input  D1,
  input  D2,
  input  D3,
  input  S0,
  input  S1,
  output out_7
);

  wire and_1_out, and_2_out, and_3_out, and_4_out, not_1_out, not_2_out, not_3_out, not_4_out;

  not not_1 (not_1_out, S0);
  not not_2 (not_2_out, S1);
  not not_3 (not_3_out, S1);
  not not_4 (not_4_out, S0);
  and and_1 (and_1_out, D0, not_1_out, not_2_out);
  and and_2 (and_2_out, D1, S0, not_3_out);
  and and_3 (and_3_out, D2, S1, not_4_out);
  and and_4 (and_4_out, D3, S1, S0);
  or or_1 (out_7, and_1_out, and_2_out, and_3_out, and_4_out);
endmodule

module SINGLE_BIT_AU (
  input  Cin,
  input  B0,
  input  A0,
  input  Constant1,
  input  S0,
  input  S1,
  output D0,
  output Carry_Out
);

  wire main_1_out_7, not_1_out, not_2_out;

  not not_1 (not_1_out, B0);
  not not_2 (not_2_out, Constant1);
  _4INTO1_MUX_main main_1 (
    .D0(B0), .D1(not_1_out), .D2(Constant1), .D3(not_2_out), .S0(S0), .S1(S1), .out_7(main_1_out_7));
  _4INTO1_MUX_FA fa_1 (.in_1(Cin), .in_2(A0), .in_3(main_1_out_7), .out_4(D0), .out_5(Carry_Out));
endmodule
