// Logisim project 4INTO1 MUX.circ as structural Verilog: 4 circuits, main circuit main
module main (
  input  D0,
  input  D1,
  input  D2,
  input  D3,
  input  S0,
  input  S1,
  output out_7
);

  wire and_1_out, and_2_out, and_3_out, and_4_out, not_1_out, not_2_out, not_3_out, not_4_out;

  not not_1 (not_1_out, S0);
  not not_2 (not_2_out, S1);
  not not_3 (not_3_out, S1);
  not not_4 (not_4_out, S0);
  and and_1 (and_1_out, D0, not_1_out, not_2_out);
  and and_2 (and_2_out, D1, S0, not_3_out);
  and and_3 (and_3_out, D2, S1, not_4_out);
  and and_4 (and_4_out, D3, S1, S0);
  or or_1 (out_7, and_1_out, and_2_out, and_3_out, and_4_out);
endmodule

module SINGLE_LOGIC (
  input  B0,
  input  A0,
  input  S1,
  input  S0,
  output out_5
);

  wire and_1_out, not_1_out, or_1_out, xor_1_out;

  and and_1 (and_1_out, A0, B0);
  or or_1 (or_1_out, A0, B0);
  xor xor_1 (xor_1_out, A0, B0);
  not not_1 (not_1_out, A0);
  main main_1 (.D0(and_1_out), .D1(or_1_out), .D2(xor_1_out), .D3(not_1_out), .S0(S0), .S1(S1), .out_7(out_5));
endmodule

module FA (
  input  in_1,
  input  in_2,
  input  in_3,
  output out_4,
  output out_5
);

  wire and_1_out, and_2_out, xor_1_out;

  xor xor_1 (xor_1_out, in_1, in_2);
  and and_1 (and_1_out, in_1, in_2);
  and and_2 (and_2_out, xor_1_out, in_3);
  xor xor_2 (out_4, xor_1_out, in_3);
  or or_1 (out_5, and_2_out, and_1_out);
endmodule

module SINGLBITAU (
  input  Cin,
  input  B0,
  input  A0,
  input  Constant1,
  input  S0,
  input  S1,
  output D0,
  output Carry_Out
);

  wire main_1_out_7, not_1_out, not_2_out;

  not not_1 (not_1_out, B0);
  not not_2 (not_2_out, Constant1);
  main main_1 (.D0(B0), .D1(not_1_out), .D2(Constant1), .D3(not_2_out), .S0(S0), .S1(S1), .out_7(main_1_out_7));
  FA fa_1 (.in_1(Cin), .in_2(A0), .in_3(main_1_out_7), .out_4(D0), .out_5(Carry_Out));
endmodule
