// Logisim project 4bit parralel adder.circ as structural Verilog: 2 circuits, main circuit FA
module FA (
  input  in_1,
  input  in_2,
  input  in_3,
  output out_4,
  output out_5
);

  wire and_1_out, and_2_out, xor_1_out;

  xor xor_1 (xor_1_out, in_1, in_2);
  and and_1 (and_1_out, in_1, in_2);
  and and_2 (and_2_out, xor_1_out, in_3);
  xor xor_2 (out_4, xor_1_out, in_3);
  or or_1 (out_5, and_1_out, and_2_out);
endmodule

module _3_BIT (
  input  Cin,
  input  [3:0] in_2,
  input  [3:0] in_3,
  output [3:0] Y3Y2Y1Y0,
  output Carry
);

  wire fa_1_out_5, fa_2_out_5, fa_3_out_5, xor_1_out, xor_2_out, xor_3_out, xor_4_out;

  xor xor_1 (xor_1_out, Cin, in_3[0]);
  xor xor_2 (xor_2_out, Cin, in_3[1]);
  buf xor_3 (xor_3_out, Cin);  // XOR_Gate
  xor xor_4 (xor_4_out, Cin, in_3[3]);
  FA fa_1 (.in_1(Cin), .in_2(in_2[0]), .in_3(xor_1_out), .out_4(Y3Y2Y1Y0[0]), .out_5(fa_1_out_5));
  FA fa_2 (.in_1(fa_1_out_5), .in_2(in_2[1]), .in_3(xor_2_out), .out_4(Y3Y2Y1Y0[1]), .out_5(fa_2_out_5));
  FA fa_3 (.in_1(fa_2_out_5), .in_2(in_2[2]), .in_3(xor_3_out), .out_4(Y3Y2Y1Y0[2]), .out_5(fa_3_out_5));
  FA fa_4 (.in_1(fa_3_out_5), .in_2(in_2[3]), .in_3(xor_4_out), .out_4(Y3Y2Y1Y0[3]), .out_5(Carry));

  assign in_3[2] = Cin;
endmodule
