// Logisim project DECODER.circ as structural Verilog: 6 circuits, main circuit Decoder
module Decoder (
  input  S0,
  input  S1,
  output D0,
  output D1,
  output D2,
  output D3
);

  wire nand_1_out, nand_2_out, nand_3_out, nand_4_out, nand_5_out, nand_6_out, nand_7_out, nand_8_out,
       nand_9_out, nand_10_out, nand_11_out, nand_12_out;

  nand nand_1 (nand_1_out, S0, S0);
  nand nand_2 (nand_2_out, S1, S1, S1);
  nand nand_3 (nand_3_out, S0, S0);
  nand nand_4 (nand_4_out, S1, S1);
  nand nand_5 (nand_5_out, S1, S1);
  nand nand_6 (nand_6_out, S0, S0);
  nand nand_7 (nand_7_out, S0, S1);
  nand nand_8 (nand_8_out, S0, S1);
  nand nand_9 (nand_9_out, nand_1_out, nand_2_out);
  nand nand_10 (nand_10_out, nand_3_out, nand_4_out);
  nand nand_11 (nand_11_out, S0, nand_5_out);
  nand nand_12 (nand_12_out, nand_6_out, S1);
  nand nand_13 (D3, nand_7_out, nand_8_out);
  nand nand_14 (D0, nand_9_out, nand_10_out);
  nand nand_15 (D1, nand_11_out, nand_11_out);
  nand nand_16 (D2, nand_12_out, nand_12_out);
endmodule

module _4TO1_MUX (
  input  D0,
  input  D1,
  input  D2,
  input  D3,
  input  S0,
  input  S1,
  output out_7
);

  wire and_1_out, and_2_out, and_3_out, and_4_out, not_1_out, not_2_out, not_3_out, not_4_out;

  not not_1 (not_1_out, S0);
  not not_2 (not_2_out, S1);
  not not_3 (not_3_out, S1);
  not not_4 (not_4_out, S0);
  and and_1 (and_1_out, D0, not_1_out, not_2_out);
  and and_2 (and_2_out, D1, S0, not_3_out);
  and and_3 (and_3_out, D2, S1, not_4_out);
  and and_4 (and_4_out, D3, S1, S0);
  or or_1 (out_7, and_1_out, and_2_out, and_3_out, and_4_out);
endmodule

module _4TO1Multibit (
  input  S0,
  input  S1,
  input  [3:0] A,
  input  [3:0] B,
  input  [3:0] C,
  input  [3:0] D,
  output [3:0] out_7
);

  _4TO1_MUX u_4to1_mux_1 (.D0(A[0]), .D1(B[0]), .D2(C[0]), .D3(D[0]), .S0(S1), .S1(S0), .out_7(out_7[0]));
  _4TO1_MUX u_4to1_mux_2 (.D0(A[1]), .D1(B[1]), .D2(C[1]), .D3(D[1]), .S0(S1), .S1(S0), .out_7(out_7[1]));
  _4TO1_MUX u_4to1_mux_3 (.D0(A[2]), .D1(B[2]), .D2(C[2]), .D3(B[3]), .S0(S1), .S1(S0), .out_7(out_7[2]));
  _4TO1_MUX u_4to1_mux_4 (.D0(A[3]), .D1(B[3]), .D2(C[3]), .D3(D[3]), .S0(S1), .S1(S0), .out_7(out_7[3]));

  assign D[2] = B[3];
endmodule

module REGISTER_FILE (
  input  [1:0] RedRead1,
  input  WriteEnable,
  input  [1:0] RegRead2,
  input  [1:0] WireSelect,
  input  [3:0] DataInput,
  output [3:0] ReadPort1,
  output [3:0] ReadPort2
);

  wire and_1_out, and_2_out, and_3_out, and_4_out, clock_1_out, decoder_1_d0, decoder_1_d1, decoder_1_d2,
       decoder_1_d3;
  wire [3:0] register_1_q, register_2_q, register_3_q, register_4_q;

  Decoder decoder_1 (
    .S0(WireSelect[0]), .S1(WireSelect[1]), .D0(decoder_1_d0), .D1(decoder_1_d1), .D2(decoder_1_d2),
    .D3(decoder_1_d3));
  and and_1 (and_1_out, WriteEnable, decoder_1_d0);
  and and_2 (and_2_out, WriteEnable, decoder_1_d1);
  and and_3 (and_3_out, WriteEnable, decoder_1_d2);
  and and_4 (and_4_out, WriteEnable, decoder_1_d3);
  Clock clock_1 (.out(clock_1_out));
  Register #(.width(4)) register_1 (.D(DataInput), .en(and_1_out), .Q(register_1_q), .clk(clock_1_out));  // open: clr
  Register #(.width(4)) register_2 (.D(DataInput), .en(and_2_out), .Q(register_2_q), .clk(clock_1_out));  // open: clr
  Register #(.width(4)) register_3 (.D(DataInput), .en(and_3_out), .Q(register_3_q), .clk(clock_1_out));  // open: clr
  Register #(.width(4)) register_4 (.D(DataInput), .en(and_4_out), .Q(register_4_q), .clk(clock_1_out));  // open: clr
  _4TO1Multibit u_4to1multibit_1 (
    .A(register_1_q), .B(register_2_q), .C(register_3_q), .D(register_4_q), .S0(RedRead1[0]),
    .S1(RedRead1[1]), .out_7(ReadPort1));
  _4TO1Multibit u_4to1multibit_2 (
    .A(register_1_q), .B(register_2_q), .C(register_3_q), .D(register_4_q), .S0(RegRead2[0]),
    .S1(RegRead2[1]), .out_7(ReadPort2));

  // Notes on the sheet:
  //   Decoder
  //   Clock
  //   Register
  //   Multibit MUX
endmodule

module COMBINED_REGISTER___ALU (
  input  [1:0] RedRead1,
  input  [2:0] in_2,
  input  WriteEnable,
  input  in_4,
  input  [1:0] RegRead2,
  input  [1:0] WireSelect,
  input  [3:0] Constant,
  input  [3:0] DataInput,
  output Overflow,
  output CarrySign,
  output [3:0] Y3Y2Y1Y0
);

  wire and_1_out, and_2_out, and_3_out, and_4_out, clock_1_out, decoder_1_d0, decoder_1_d1, decoder_1_d2,
       decoder_1_d3;
  wire [3:0] n4to1multibit_1_out_7, n4to1multibit_2_out_7, register_1_q, register_2_q, register_3_q,
       register_4_q;

  Decoder decoder_1 (
    .S0(WireSelect[0]), .S1(WireSelect[1]), .D0(decoder_1_d0), .D1(decoder_1_d1), .D2(decoder_1_d2),
    .D3(decoder_1_d3));
  and and_1 (and_1_out, WriteEnable, decoder_1_d0);
  and and_2 (and_2_out, WriteEnable, decoder_1_d1);
  and and_3 (and_3_out, WriteEnable, decoder_1_d2);
  and and_4 (and_4_out, WriteEnable, decoder_1_d3);
  Clock clock_1 (.out(clock_1_out));
  Register #(.width(4)) register_1 (.D(DataInput), .en(and_1_out), .Q(register_1_q), .clk(clock_1_out));  // open: clr
  Register #(.width(4)) register_2 (.D(DataInput), .en(and_2_out), .Q(register_2_q), .clk(clock_1_out));  // open: clr
  Register #(.width(4)) register_3 (.D(DataInput), .en(and_3_out), .Q(register_3_q), .clk(clock_1_out));  // open: clr
  Register #(.width(4)) register_4 (.D(DataInput), .en(and_4_out), .Q(register_4_q), .clk(clock_1_out));  // open: clr
  _4TO1Multibit u_4to1multibit_1 (
    .A(register_1_q), .B(register_2_q), .C(register_3_q), .D(register_4_q), .S0(RedRead1[0]),
    .S1(RedRead1[1]), .out_7(n4to1multibit_1_out_7));
  _4TO1Multibit u_4to1multibit_2 (
    .A(register_1_q), .B(register_2_q), .C(register_3_q), .D(register_4_q), .S0(RegRead2[0]),
    .S1(RegRead2[1]), .out_7(n4to1multibit_2_out_7));
  _4_BIT_ALU u_4_bit_alu_1 (
    .B(n4to1multibit_1_out_7), .Cin(in_4), .A(n4to1multibit_2_out_7), .Constant(Constant), .S2(in_2[2]),
    .S1(in_2[1]), .S0(in_2[0]), .Overflow(Overflow), .Y(Y3Y2Y1Y0), .Carry___Sign(CarrySign));

  // Notes on the sheet:
  //   Decoder
  //   Clock
  //   Register
  //   Multibit MUX
  //   ALU
endmodule

module _4_BIT_ALU (
  input  [3:0] B,
  input  Cin,
  input  [3:0] A,
  input  S2,
  input  S1,
  input  S0,
  input  [3:0] Constant,
  output Overflow,
  output [3:0] Y,
  output Carry___Sign
);

  wire [3:0] n4_bit_au_1_out_7, n4bit_logic_lu_1_y3y2y1y0;

  _4_BIT_AU u_4_bit_au_1 (
    .Cin(Cin), .B3B2B1B0(B), .A3A2A1A0(A), .Constant(Constant), .in_5(S1), .in_6(S0),
    .out_7(n4_bit_au_1_out_7), .OVERFLOW(Overflow), .CarryCut(Carry___Sign));
  _4BIT_Logic_LU u_4bit_logic_lu_1 (.B3B2B1B0(B), .in_4(A), .S1(S1), .S0(S0), .Y3Y2Y1Y0(n4bit_logic_lu_1_y3y2y1y0));
  _2to1MultibitMux u_2to1multibitmux_1 (.A(n4_bit_au_1_out_7), .B(n4bit_logic_lu_1_y3y2y1y0), .in_3(S2), .Y(Y));

  // Notes on the sheet:
  //   4 bit AU
  //   4 BIT AU
  //   2 to 1multibit MUX
endmodule
