// Logisim project lab7.circ as structural Verilog
module _2to1MUX_singlebit (
  input  D0,
  input  D1,
  input  S0,
  output Y
);

  wire nand_1_out, nand_2_out, nand_3_out;

  nand nand_1 (nand_1_out, S0, S0);
  nand nand_2 (nand_2_out, nand_1_out, D0);
  nand nand_3 (nand_3_out, S0, D1);
  nand nand_4 (Y, nand_2_out, nand_3_out);
endmodule

module _2to1Multimux (
  input  [3:0] A,
  input  [3:0] B,
  input  in_3,
  output [3:0] Y
);

  _2to1MUX_singlebit u_2to1mux_singlebit_1 (.D0(A[0]), .D1(B[0]), .S0(in_3), .Y(Y[0]));
  _2to1MUX_singlebit u_2to1mux_singlebit_2 (.D0(A[1]), .D1(B[1]), .S0(in_3), .Y(Y[1]));
  _2to1MUX_singlebit u_2to1mux_singlebit_3 (.D0(A[2]), .D1(B[2]), .S0(in_3), .Y(Y[2]));
  _2to1MUX_singlebit u_2to1mux_singlebit_4 (.D0(A[3]), .D1(B[3]), .S0(in_3), .Y(Y[3]));
endmodule

module Realization_of_Q_register (
  input  EN,
  input  CLR
);

  wire clock_1_out, d_ff_1_q, d_ff_2_q, d_ff_3_q, d_ff_4_q, undriven;

  Clock clock_1 (.out(clock_1_out));
  D_Flip_Flop d_ff_1 (.clk(clock_1_out), .D(undriven), .Q(d_ff_1_q), .en(EN), .reset(CLR));  // open: Qn, preset
  D_Flip_Flop d_ff_2 (.clk(clock_1_out), .D(d_ff_1_q), .Q(d_ff_2_q), .en(EN), .reset(CLR));  // open: Qn, preset
  D_Flip_Flop d_ff_3 (.clk(clock_1_out), .D(d_ff_2_q), .Q(d_ff_3_q), .en(EN), .reset(CLR));  // open: Qn, preset
  D_Flip_Flop d_ff_4 (.clk(clock_1_out), .D(d_ff_3_q), .Q(d_ff_4_q), .en(EN), .reset(CLR));  // open: Qn, preset

  // Notes on the sheet:
  //   Clock
  //   To select pin of multibit MUX
endmodule

module Realization_of_Accumulator (
  input  EN,
  input  CLR,
  output [3:0] Output
);

  wire clock_1_out, undriven, undriven_2, undriven_3, undriven_4;

  Clock clock_1 (.out(clock_1_out));
  D_Flip_Flop d_ff_1 (.clk(clock_1_out), .D(undriven), .Q(Output[3]), .en(EN), .reset(CLR));  // open: Qn, preset
  D_Flip_Flop d_ff_2 (.clk(clock_1_out), .D(undriven_2), .Q(Output[2]), .en(EN), .reset(CLR));  // open: Qn, preset
  D_Flip_Flop d_ff_3 (.clk(clock_1_out), .D(undriven_3), .Q(Output[1]), .en(EN), .reset(CLR));  // open: Qn, preset
  D_Flip_Flop d_ff_4 (.clk(clock_1_out), .D(undriven_4), .Q(Output[0]), .en(EN), .reset(CLR));  // open: Qn, preset

  // Notes on the sheet:
  //   CLK
  //   Connect to the output of each 2:1 singlle bit MUX
  //   To D input of MSB of Q register
endmodule

module Inerconnection_of_different_blocks (
  input  in_1,
  input  in_2,
  input  in_3,
  output out_4
);

  wire n2to1mux_singlebit_1_y, n2to1mux_singlebit_2_y, n2to1mux_singlebit_3_y, n2to1mux_singlebit_4_y,
       undriven, undriven_2, undriven_3;
  wire [3:0] parallel_adder_1_y3y2y1y0, undriven_4, undriven_5;

  _2to1MUX_singlebit u_2to1mux_singlebit_1 (
    .D0(in_2), .D1(parallel_adder_1_y3y2y1y0[3]), .S0(in_1), .Y(n2to1mux_singlebit_1_y));
  _2to1MUX_singlebit u_2to1mux_singlebit_2 (
    .D0(undriven), .D1(parallel_adder_1_y3y2y1y0[2]), .S0(in_1), .Y(n2to1mux_singlebit_2_y));
  _2to1MUX_singlebit u_2to1mux_singlebit_3 (
    .D0(undriven_2), .D1(parallel_adder_1_y3y2y1y0[1]), .S0(in_1), .Y(n2to1mux_singlebit_3_y));
  parallel_adder parallel_adder_1 (
    .in_2(undriven_4), .in_3(undriven_5), .Cin(in_3), .Y3Y2Y1Y0(parallel_adder_1_y3y2y1y0), .Carry(out_4));
  _2to1MUX_singlebit u_2to1mux_singlebit_4 (
    .D0(undriven_3), .D1(parallel_adder_1_y3y2y1y0[0]), .S0(in_1), .Y(n2to1mux_singlebit_4_y));
endmodule

module FA (
  input  in_1,
  input  in_2,
  input  in_3,
  output out_4,
  output out_5
);

  wire and_1_out, and_2_out, xor_1_out;

  xor xor_1 (xor_1_out, in_1, in_2);
  and and_1 (and_1_out, in_1, in_2);
  and and_2 (and_2_out, xor_1_out, in_3);
  xor xor_2 (out_4, xor_1_out, in_3);
  or or_1 (out_5, and_1_out, and_2_out);
endmodule

module parallel_adder (
  input  Cin,
  input  [3:0] in_2,
  input  [3:0] in_3,
  output [3:0] Y3Y2Y1Y0,
  output Carry
);

  wire fa_1_out_5, fa_2_out_5, fa_3_out_5, xor_1_out, xor_2_out, xor_3_out, xor_4_out;

  xor xor_1 (xor_1_out, Cin, in_3[0]);
  xor xor_2 (xor_2_out, Cin, in_3[1]);
  buf xor_3 (xor_3_out, Cin);  // XOR_Gate
  xor xor_4 (xor_4_out, Cin, in_3[3]);
  FA fa_1 (.in_1(Cin), .in_2(in_2[0]), .in_3(xor_1_out), .out_4(Y3Y2Y1Y0[0]), .out_5(fa_1_out_5));
  FA fa_2 (.in_1(fa_1_out_5), .in_2(in_2[1]), .in_3(xor_2_out), .out_4(Y3Y2Y1Y0[1]), .out_5(fa_2_out_5));
  FA fa_3 (.in_1(fa_2_out_5), .in_2(in_2[2]), .in_3(xor_3_out), .out_4(Y3Y2Y1Y0[2]), .out_5(fa_3_out_5));
  FA fa_4 (.in_1(fa_3_out_5), .in_2(in_2[3]), .in_3(xor_4_out), .out_4(Y3Y2Y1Y0[3]), .out_5(Carry));

  assign in_3[2] = Cin;
endmodule

module Complete_Circuit (
  input  EN,
  input  CLR,
  input  EN_2,
  input  CLR_2,
  input  S,
  input  Data,
  input  Cin,
  input  [3:0] Bunch_of_Zeros,
  input  [3:0] Multiplicand,
  output [3:0] Output,
  output [3:0] Y,
  output Cout,
  output [3:0] Y_2
);

  wire clock_1_out, d_ff_5_q, d_ff_6_q, d_ff_7_q, d_ff_8_q, n2to1mux_singlebit_1_y, n2to1mux_singlebit_2_y,
       n2to1mux_singlebit_3_y, n2to1mux_singlebit_4_y;

  Clock clock_1 (.out(clock_1_out));
  _2to1MUX_singlebit u_2to1mux_singlebit_1 (.D0(Data), .D1(Y_2[3]), .S0(S), .Y(n2to1mux_singlebit_1_y));
  D_Flip_Flop d_ff_1 (
    .clk(clock_1_out), .D(n2to1mux_singlebit_1_y), .Q(Output[3]), .en(EN_2), .reset(CLR_2));  // open: Qn, preset
  D_Flip_Flop d_ff_2 (
    .clk(clock_1_out), .D(n2to1mux_singlebit_2_y), .Q(Output[2]), .en(EN_2), .reset(CLR_2));  // open: Qn, preset
  _2to1MUX_singlebit u_2to1mux_singlebit_2 (.D0(Output[3]), .D1(Y_2[2]), .S0(S), .Y(n2to1mux_singlebit_2_y));
  _2to1MUX_singlebit u_2to1mux_singlebit_3 (.D0(Output[2]), .D1(Y_2[1]), .S0(S), .Y(n2to1mux_singlebit_3_y));
  D_Flip_Flop d_ff_3 (
    .clk(clock_1_out), .D(n2to1mux_singlebit_3_y), .Q(Output[1]), .en(EN_2), .reset(CLR_2));  // open: Qn, preset
  _2to1MUX_singlebit u_2to1mux_singlebit_4 (.D0(Output[1]), .D1(Output[1]), .S0(S), .Y(n2to1mux_singlebit_4_y));
  parallel_adder parallel_adder_1 (.in_2(Y), .in_3(Output), .Cin(Cin), .Y3Y2Y1Y0({Y_2[3:1], Output[1]}), .Carry(Cout));
  D_Flip_Flop d_ff_4 (
    .clk(clock_1_out), .D(n2to1mux_singlebit_4_y), .Q(Output[0]), .en(EN_2), .reset(CLR_2));  // open: Qn, preset
  D_Flip_Flop d_ff_5 (.clk(clock_1_out), .D(Output[0]), .Q(d_ff_5_q), .en(EN), .reset(CLR));  // open: Qn, preset
  D_Flip_Flop d_ff_6 (.clk(clock_1_out), .D(d_ff_5_q), .Q(d_ff_6_q), .en(EN), .reset(CLR));  // open: Qn, preset
  D_Flip_Flop d_ff_7 (.clk(clock_1_out), .D(d_ff_6_q), .Q(d_ff_7_q), .en(EN), .reset(CLR));  // open: Qn, preset
  D_Flip_Flop d_ff_8 (.clk(clock_1_out), .D(d_ff_7_q), .Q(d_ff_8_q), .en(EN), .reset(CLR));  // open: Qn, preset
  _2to1Multimux u_2to1multimux_1 (.A(Bunch_of_Zeros), .B(Multiplicand), .in_3(d_ff_8_q), .Y(Y));

  assign Y_2[0] = Output[1];

  // Notes on the sheet:
  //   CLOCK
endmodule
